// Logisim project assignment 1 copy.circ as structural Verilog: 1 circuit, main circuit main
module main (
  input  A3,
  input  B3,
  input  A2,
  input  B2,
  input  A1,
  input  B1,
  input  A0,
  input  B0,
  input  A3_2,
  input  B3_2,
  input  A2_2,
  input  B2_2,
  input  A1_2,
  input  B1_2,
  input  A0_2,
  input  B0_2,
  input  C0,
  output A_B,
  output A_B_2,
  output A_B_3,
  output C4,
  output S3,
  output S2,
  output S1,
  output S0
);

  wire and_1_out, and_2_out, and_3_out, and_4_out, and_5_out, and_6_out, and_7_out, and_8_out, and_9_out,
       and_10_out, and_11_out, and_12_out, and_13_out, and_14_out, and_15_out, and_16_out, and_17_out,
       and_18_out, and_20_out, not_1_out, not_2_out, not_3_out, not_4_out, not_5_out, not_6_out, not_7_out,
       not_8_out, or_1_out, or_2_out, or_3_out, xnor_1_out, xnor_2_out, xnor_3_out, xnor_4_out, xor_1_out,
       xor_2_out, xor_3_out, xor_4_out;

  xor xor_1 (xor_1_out, A3_2, B3_2);
  and and_1 (and_1_out, A3_2, B3_2);
  xor xor_2 (xor_2_out, A2_2, B2_2);
  and and_2 (and_2_out, A2_2, B2_2);
  xor xor_3 (xor_3_out, A1_2, B1_2);
  and and_3 (and_3_out, A1_2, B1_2);
  xor xor_4 (xor_4_out, A0_2, B0_2);
  and and_4 (and_4_out, A0_2, B0_2);
  xnor xnor_1 (xnor_1_out, A3, B3);
  xnor xnor_2 (xnor_2_out, A2, B2);
  xnor xnor_3 (xnor_3_out, A1, B1);
  xnor xnor_4 (xnor_4_out, A0, B0);
  not not_1 (not_1_out, B3);
  not not_2 (not_2_out, B2);
  not not_3 (not_3_out, B1);
  not not_4 (not_4_out, B0);
  not not_5 (not_5_out, A3);
  not not_6 (not_6_out, A2);
  not not_7 (not_7_out, A1);
  not not_8 (not_8_out, A0);
  and and_5 (and_5_out, C0, xor_2_out, xor_4_out, xor_3_out);
  and and_6 (and_6_out, xor_2_out, xor_3_out, and_4_out);
  and and_7 (and_7_out, xor_2_out, and_3_out);
  and and_8 (and_8_out, C0, xor_3_out, xor_4_out);
  and and_9 (and_9_out, xor_3_out, and_4_out);
  and and_10 (and_10_out, C0, xor_4_out);
  and and_11 (and_11_out, A3, not_1_out);
  and and_12 (and_12_out, xnor_1_out, A2, not_2_out);
  and and_13 (and_13_out, xnor_2_out, xnor_1_out, A1, not_3_out);
  and and_14 (and_14_out, xnor_2_out, xnor_3_out, xnor_1_out, A0, not_4_out);
  and and_15 (and_15_out, B3, not_5_out);
  and and_16 (and_16_out, xnor_1_out, B2, not_6_out);
  and and_17 (and_17_out, xnor_2_out, xnor_1_out, B1, not_7_out);
  and and_18 (and_18_out, xnor_3_out, xnor_2_out, xnor_1_out, B0, not_8_out);
  or or_1 (or_1_out, and_5_out, and_6_out, and_7_out, and_2_out);
  or or_2 (or_2_out, and_8_out, and_9_out, and_3_out);
  or or_3 (or_3_out, and_10_out, and_4_out);
  or or_4 (A_B, and_11_out, and_12_out, and_13_out, and_14_out);
  and and_19 (A_B_2, xnor_1_out, xnor_2_out, xnor_3_out, xnor_4_out);
  or or_5 (A_B_3, and_15_out, and_16_out, and_17_out, and_18_out);
  and and_20 (and_20_out, xor_1_out, or_1_out);
  or or_6 (C4, and_1_out, and_20_out);
  xor xor_5 (S3, xor_1_out, or_1_out);
  xor xor_6 (S2, xor_2_out, or_2_out);
  xor xor_7 (S1, xor_3_out, or_3_out);
  xor xor_8 (S0, xor_4_out, C0);

  // Notes on the sheet:
  //   P3
  //   G3
  //   P2
  //   G2
  //   P1
  //   G1
  //   P0
  //   G0
  //   ASSIGNMENT 1: 4 BIT MAGNITUDE COMPARATOR
  //   ASSIGNMENT 1: CARRY LOOK AHEAD ADDER
endmodule
