// Logisim project 2'sComplement(4bit).circ as structural Verilog: 1 circuit, main circuit main
module main (
  input  [3:0] in_1,
  output [3:0] out_2,
  output out_3
);

  wire [0:0] not_2_out;
  wire [3:0] not_1_out;

  assign not_1_out = ~in_1;  // NOT_Gate not_1, 4 bits wide
  not not_2 (not_2_out[0], 1'b0);
  Adder #(.width(4)) adder_1 (.a(not_1_out), .b({3'b000, not_2_out[0]}), .out(out_2), .cout(out_3));  // open: cin
endmodule
