// Logisim project 9sComplementOfBinaryNumbers.circ as structural Verilog: 1 circuit, main circuit main
module main (
  input  [3:0] in_1,
  input  [3:0] in_2,
  input  [3:0] in_3,
  input  [3:0] in_4,
  input  [3:0] in_5,
  output [3:0] out_6,
  output [3:0] out_7,
  output [3:0] out_8,
  output K,
  output [3:0] out_10,
  output [3:0] out_11
);

  wire [0:0] not_5_out;
  wire [3:0] adder_1_out, not_1_out, not_4_out;
  wire [3:1] not_2_out;

  Subtractor #(.width(4)) subtractor_1 (.a(4'b1001), .b(in_2), .out(out_7));  // open: bin, bout
  Subtractor #(.width(4)) subtractor_2 (.a(4'b1001), .b(in_3), .out(out_8));  // open: bin, bout
  Subtractor #(.width(4)) subtractor_3 (.a(4'b1001), .b(in_4), .out(out_10));  // open: bin, bout
  Subtractor #(.width(4)) subtractor_4 (.a(4'b1001), .b(in_5), .out(out_11));  // open: bin, bout
  assign not_1_out = ~in_1;  // NOT_Gate not_1, 4 bits wide
  not not_2 (not_2_out[1], 1'b0);
  not not_3 (not_2_out[3], 1'b0);
  Adder #(.width(4)) adder_1 (
    .a(not_1_out), .b({not_2_out[3], 1'b0, not_2_out[1], 1'b0}), .out(adder_1_out), .cout(K));  // open: cin
  assign not_4_out = ~adder_1_out;  // NOT_Gate not_4, 4 bits wide
  not not_5 (not_5_out[0], 1'b0);
  Adder #(.width(4)) adder_2 (.a(not_4_out), .b({3'b000, not_5_out[0]}), .out(out_6));  // open: cin, cout

  // Notes on the sheet:
  //   9's Complement of Decimal numbers
  //   9's Complement of Binary numbers
  //   If the carry K is zero then the final answer is negetive otherwise positive.
endmodule
