// Logisim project 2421toBCD.circ as structural Verilog: 1 circuit, main circuit main
module main (
  input  W,
  input  X,
  input  Y,
  input  Z,
  output S1,
  output S2,
  output S3,
  output S4
);

  wire and_1_out, and_2_out, not_1_out, not_2_out;

  not not_1 (not_1_out, X);
  not not_2 (not_2_out, Y);
  and and_1 (and_1_out, X, not_2_out);
  and and_2 (and_2_out, W, not_1_out);
  and and_3 (S1, Y, X);
  or or_1 (S2, and_1_out, and_2_out);
  xor xor_1 (S3, W, Y);

  assign S4 = Z;

  // Notes on the sheet:
  //   2421 to BCD
endmodule
