// Logisim project que3.circ as structural Verilog: 1 circuit, main circuit main
module main (
  input  A,
  input  B,
  input  C,
  input  D,
  output F
);

  wire not_1_out, not_2_out, not_3_out, not_4_out, or_1_out, or_2_out, or_3_out;

  not not_1 (not_1_out, A);
  not not_2 (not_2_out, B);
  not not_3 (not_3_out, C);
  not not_4 (not_4_out, D);
  or or_1 (or_1_out, not_1_out, B, not_3_out, D);
  or or_2 (or_2_out, A, not_2_out, not_3_out, D);
  or or_3 (or_3_out, not_1_out, not_2_out, not_4_out);
  and and_1 (F, or_1_out, or_2_out, or_3_out);

  // Notes on the sheet:
  //   F = (A' + B + C' + D)(A+B'+C'+D)(A'+B'+D')
endmodule
