// Logisim project SR-flipflop.circ as structural Verilog: 1 circuit, main circuit main
module main (
  input  S,
  input  CLK,
  input  R,
  input  R_2,
  input  CLK_2,
  input  S_2,
  output Q,
  output Q_prime,
  output Q_2,
  output Q_prime_2
);

  wire nand_1_out, nand_2_out, nor_1_out, nor_2_out;

  nand nand_1 (nand_1_out, S, CLK);
  nand nand_2 (nand_2_out, CLK, R);
  nor nor_1 (nor_1_out, R_2, CLK_2);
  nor nor_2 (nor_2_out, CLK_2, S_2);
  nand nand_3 (Q, nand_1_out, Q_prime);
  nand nand_4 (Q_prime, Q, nand_2_out);
  nor nor_3 (Q_2, nor_1_out, Q_prime_2);
  nor nor_4 (Q_prime_2, Q_2, nor_2_out);

  // Notes on the sheet:
  //   SR Flip Flop - with and gate
  //   SR Flip Flop - with or gate
endmodule
