// Logisim project booleanFunction.circ as structural Verilog: 1 circuit, main circuit main
module main (
  input  D,
  input  [2:0] D_2,
  output F___BC___ABD_prime___A_prime_C_prime_D
);

  wire not_1_out, not_2_out;

  not not_1 (not_1_out, 1'b0);
  not not_2 (not_2_out, D);
  Multiplexer #(.select(3)) multiplexer_1 (
    .in0(D), .in1(1'b0), .in2(1'b0), .in3(not_1_out), .in4(1'b0), .in5(1'b0), .in6(not_2_out),
    .in7(not_1_out), .out(F___BC___ABD_prime___A_prime_C_prime_D), .sel(D_2));  // open: en

  // Notes on the sheet:
  //   Implementation of boolean function using Multiplexer
endmodule
