// Logisim project practical1.circ as structural Verilog: 1 circuit, main circuit main
module main (
  input  A,
  input  A_2,
  input  B,
  input  A_3,
  input  B_2,
  input  A_4,
  input  B_3,
  input  A_5,
  input  B_4,
  input  A_6,
  input  B_5,
  input  A_7,
  input  B_6,
  output \Ā ,
  output A_B,
  output A_B_2,
  output A_B__whole_bar,
  output A_B__whole_bar_2,
  output A__B_bar____A_bar__B,
  output A_B_____A_bar____B_bar
);

  not not_1 (\Ā , A);
  and and_1 (A_B, A_2, B);
  or or_1 (A_B_2, A_3, B_2);
  nand nand_1 (A_B__whole_bar, A_4, B_3);
  nor nor_1 (A_B__whole_bar_2, A_5, B_4);
  xor xor_1 (A__B_bar____A_bar__B, A_6, B_5);
  xnor xnor_1 (A_B_____A_bar____B_bar, A_7, B_6);

  // Notes on the sheet:
  //   NOT gate
  //   AND gate
  //   OR gate
  //   NAND gate
  //   NOR gate
  //   XOR gate
  //   XNOR gate
endmodule
