// Logisim project practical2.circ as structural Verilog: 1 circuit, main circuit main
module main (
  input  A,
  input  A_2,
  input  A_3,
  input  A_4,
  input  A_5,
  input  A_6,
  input  B,
  input  B_2,
  input  B_3,
  input  A_7,
  input  A_8,
  input  A_9,
  input  B_4,
  input  B_5,
  input  B_6,
  input  A_10,
  input  A_11,
  input  A_12,
  input  B_7,
  input  B_8,
  input  B_9,
  input  A_13,
  input  A_14,
  input  A_15,
  input  B_10,
  input  B_11,
  input  B_12,
  input  A_16,
  input  A_17,
  input  A_18,
  input  B_13,
  input  B_14,
  input  B_15,
  input  A_19,
  input  A_20,
  input  A_21,
  input  B_16,
  input  B_17,
  input  B_18,
  output \Ā ,
  output A_not,
  output A_not_2,
  output A_B,
  output A_B_2,
  output A_and_B,
  output A_or_B,
  output A_or_B_2,
  output A_B_3,
  output A_B__whole_bar,
  output A_B__whole_bar_2,
  output A_B__whole_bar_3,
  output A_B__whole_bar_4,
  output A_B__whole_bar_5,
  output A_B__whole_bar_6,
  output A_xor_B,
  output A__B_bar____A_bar__B,
  output A_xor_B_2,
  output A_xnor_B,
  output A_B_____A_bar____B_bar,
  output A_xnor_B_2
);

  wire A_and_B_bar_2_out, A_and_B_bar_out, A_bar_2_out, A_bar__and_B_2_out, A_bar__and_B_out, A_bar_out,
       B_bar_2_out, B_bar_out, nand_3_out, nand_4_out, nand_5_out, nand_9_out, nand_10_out, nand_11_out,
       nand_13_out, nand_14_out, nand_15_out, nand_16_out, nand_17_out, nand_18_out, nand_19_out,
       nand_20_out, nand_22_out, nor_3_out, nor_4_out, nor_5_out, nor_7_out, nor_8_out, nor_10_out,
       nor_13_out, nor_14_out, nor_15_out, nor_16_out, nor_17_out, nor_18_out, nor_19_out, nor_20_out,
       nor_21_out, nor_22_out, nor_23_out, nor_24_out, nor_25_out, nor_26_out, nor_27_out, nor_28_out,
       nor_29_out;

  not not_1 (\Ā , A);
  and and_1 (A_B, A_5, B);
  or or_1 (A_B_3, A_9, B_5);
  nand nand_1 (A_B__whole_bar, A_11, B_7);
  nor nor_1 (A_B__whole_bar_4, A_14, B_10);
  xor xor_1 (A__B_bar____A_bar__B, A_18, B_13);
  xnor xnor_1 (A_B_____A_bar____B_bar, A_21, B_16);
  nand nand_2 (A_not, A_2, A_2);
  nand nand_3 (nand_3_out, A_6, B_2);
  nand nand_4 (nand_4_out, A_7, A_7);
  nand nand_5 (nand_5_out, B_6, B_6);
  nand nand_6 (A_B_2, nand_3_out, nand_3_out);
  nand nand_7 (A_or_B, nand_4_out, nand_5_out);
  nand nand_8 (A_B__whole_bar_2, A_12, B_8);
  nand nand_9 (nand_9_out, A_13, A_13);
  nand nand_10 (nand_10_out, B_12, B_12);
  nand A_bar (A_bar_out, A_16, A_16);
  nand B_bar (B_bar_out, B_14, B_14);
  nand A_bar_2 (A_bar_2_out, A_19, A_19);
  nand B_bar_2 (B_bar_2_out, B_17, B_17);
  nand nand_11 (nand_11_out, nand_9_out, nand_10_out);
  nand nand_12 (A_B__whole_bar_5, nand_11_out, nand_11_out);
  nand nand_13 (nand_13_out, A_bar_out, B_14);
  nand nand_14 (nand_14_out, A_16, B_bar_out);
  nand nand_15 (nand_15_out, A_bar_2_out, B_17);
  nand nand_16 (nand_16_out, A_19, B_bar_2_out);
  nor nor_2 (A_not_2, A_3, A_3);
  nor nor_3 (nor_3_out, A_4, A_4);
  nor nor_4 (nor_4_out, B_3, B_3);
  nor nor_5 (nor_5_out, A_8, B_4);
  nand A_bar__and_B (A_bar__and_B_out, nand_13_out, nand_13_out);
  nand A_and_B_bar (A_and_B_bar_out, nand_14_out, nand_14_out);
  nand A_bar__and_B_2 (A_bar__and_B_2_out, nand_15_out, nand_15_out);
  nand A_and_B_bar_2 (A_and_B_bar_2_out, nand_16_out, nand_16_out);
  nor nor_6 (A_and_B, nor_3_out, nor_4_out);
  nor nor_7 (nor_7_out, A_10, A_10);
  nor nor_8 (nor_8_out, B_9, B_9);
  nand nand_17 (nand_17_out, A_bar__and_B_out, A_bar__and_B_out);
  nand nand_18 (nand_18_out, A_and_B_bar_out, A_and_B_bar_out);
  nand nand_19 (nand_19_out, A_bar__and_B_2_out, A_bar__and_B_2_out);
  nand nand_20 (nand_20_out, A_and_B_bar_2_out, A_and_B_bar_2_out);
  nor nor_9 (A_or_B_2, nor_5_out, nor_5_out);
  nor nor_10 (nor_10_out, nor_7_out, nor_8_out);
  nand nand_21 (A_xor_B, nand_17_out, nand_18_out);
  nand nand_22 (nand_22_out, nand_19_out, nand_20_out);
  nor nor_11 (A_B__whole_bar_3, nor_10_out, nor_10_out);
  nor nor_12 (A_B__whole_bar_6, A_15, B_11);
  nand nand_23 (A_xnor_B, nand_22_out, nand_22_out);
  nor nor_13 (nor_13_out, A_17, A_17);
  nor nor_14 (nor_14_out, B_15, B_15);
  nor nor_15 (nor_15_out, A_20, A_20);
  nor nor_16 (nor_16_out, B_18, B_18);
  nor nor_17 (nor_17_out, nor_13_out, nor_13_out);
  nor nor_18 (nor_18_out, B_15, B_15);
  nor nor_19 (nor_19_out, A_17, A_17);
  nor nor_20 (nor_20_out, nor_14_out, nor_14_out);
  nor nor_21 (nor_21_out, nor_15_out, nor_15_out);
  nor nor_22 (nor_22_out, B_18, B_18);
  nor nor_23 (nor_23_out, A_20, A_20);
  nor nor_24 (nor_24_out, nor_16_out, nor_16_out);
  nor nor_25 (nor_25_out, nor_17_out, nor_18_out);
  nor nor_26 (nor_26_out, nor_19_out, nor_20_out);
  nor nor_27 (nor_27_out, nor_25_out, nor_26_out);
  nor nor_28 (nor_28_out, nor_21_out, nor_22_out);
  nor nor_29 (nor_29_out, nor_23_out, nor_24_out);
  nor nor_30 (A_xor_B_2, nor_27_out, nor_27_out);
  nor nor_31 (A_xnor_B_2, nor_28_out, nor_29_out);

  // Notes on the sheet:
  //   GATES
  //   NAND
  //   NOR
endmodule
