// Logisim project practical3-19BCE245.circ as structural Verilog: 1 circuit, main circuit main
module main (
  input  A,
  input  B,
  input  A_2,
  input  B_2,
  input  C,
  input  A_3,
  input  B_3,
  input  A_4,
  input  B_4,
  input  C_2,
  output Sum,
  output Carry,
  output Sum_2,
  output Carry_2,
  output Difference,
  output Borrow,
  output Difference_2,
  output Borrow_2
);

  wire and_2_out, and_3_out, and_5_out, and_6_out, not_1_out, not_2_out, not_3_out, xor_3_out, xor_4_out;

  xor xor_1 (Sum, A, B);
  and and_1 (Carry, A, B);
  xor xor_2 (Difference, A_3, B_3);
  not not_1 (not_1_out, A_3);
  xor xor_3 (xor_3_out, A_2, B_2);
  and and_2 (and_2_out, xor_3_out, C);
  and and_3 (and_3_out, A_2, B_2);
  and and_4 (Borrow, not_1_out, B_3);
  xor xor_4 (xor_4_out, A_4, B_4);
  not not_2 (not_2_out, xor_4_out);
  not not_3 (not_3_out, A_4);
  xor xor_5 (Sum_2, xor_3_out, C);
  or or_1 (Carry_2, and_2_out, and_3_out);
  xor xor_6 (Difference_2, xor_4_out, C_2);
  and and_5 (and_5_out, not_2_out, C_2);
  and and_6 (and_6_out, not_3_out, B_4);
  or or_2 (Borrow_2, and_5_out, and_6_out);

  // Notes on the sheet:
  //   Half Adder
  //   Half Subtractor
  //   Full Adder
  //   Full Subtractor
endmodule
