// Logisim project 4 bit incrementor.circ as structural Verilog: 1 circuit, main circuit main
module main (
  input  _1,
  input  a1,
  input  a2,
  input  a3,
  input  a4,
  output out_6,
  output out_7,
  output out_8,
  output out_9
);

  wire adder_1_cout, adder_2_cout, adder_3_cout;

  Adder #(.width(1)) adder_1 (.b(a1), .out(out_6), .cin(_1), .cout(adder_1_cout));  // open: a
  Adder #(.width(1)) adder_2 (.b(a2), .out(out_7), .cin(adder_1_cout), .cout(adder_2_cout));  // open: a
  Adder #(.width(1)) adder_3 (.b(a3), .out(out_8), .cin(adder_2_cout), .cout(adder_3_cout));  // open: a
  Adder #(.width(1)) adder_4 (.b(a4), .out(out_9), .cin(adder_3_cout));  // open: a, cout

  // Notes on the sheet:
  //   0110
  //   0001
  //   0111
endmodule
