// Logisim project Adder + Subtractor.circ as structural Verilog: 1 circuit, main circuit main
module main (
  input  K,
  input  A1,
  input  B1,
  input  A2,
  input  B2,
  input  in_6,
  input  B3,
  input  A4,
  input  B4,
  output S1,
  output S2,
  output S3,
  output S4,
  output Carry
);

  wire adder_1_cout, adder_2_cout, adder_3_cout, xor_1_out, xor_2_out, xor_3_out, xor_4_out;

  xor xor_1 (xor_1_out, K, B1);
  xor xor_2 (xor_2_out, K, B2);
  xor xor_3 (xor_3_out, K, B3);
  xor xor_4 (xor_4_out, K, B4);
  Adder #(.width(1)) adder_1 (.a(A1), .b(xor_1_out), .out(S1), .cin(K), .cout(adder_1_cout));
  Adder #(.width(1)) adder_2 (.a(A2), .b(xor_2_out), .out(S2), .cin(adder_1_cout), .cout(adder_2_cout));
  Adder #(.width(1)) adder_3 (.a(in_6), .b(xor_3_out), .out(S3), .cin(adder_2_cout), .cout(adder_3_cout));
  Adder #(.width(1)) adder_4 (.a(A4), .b(xor_4_out), .out(S4), .cin(adder_3_cout), .cout(Carry));
endmodule
