// Logisim project Using 4 full adders.circ as structural Verilog: 1 circuit, main circuit main
module main (
  input  _1,
  input  A,
  input  _1_2,
  input  B,
  input  _1_3,
  input  C,
  input  _1_4,
  input  D,
  output E,
  output F,
  output G,
  output H
);

  wire adder_1_cout, adder_2_cout, adder_3_cout;

  Adder #(.width(1)) adder_1 (.a(_1), .b(A), .out(E), .cout(adder_1_cout));  // open: cin
  Adder #(.width(1)) adder_2 (.a(_1_2), .b(B), .out(F), .cin(adder_1_cout), .cout(adder_2_cout));
  Adder #(.width(1)) adder_3 (.a(_1_3), .b(C), .out(G), .cin(adder_2_cout), .cout(adder_3_cout));
  Adder #(.width(1)) adder_4 (.a(_1_4), .b(D), .out(H), .cin(adder_3_cout));  // open: cout
endmodule
