// Logisim project subtractor.circ as structural Verilog: 1 circuit, main circuit main
module main (
  input  in_1,
  input  in_2,
  input  in_3,
  input  in_4,
  input  in_5,
  output out_6,
  output out_7,
  output out_8,
  output out_9
);

  wire subtractor_1_bout, subtractor_2_bout, subtractor_3_bout;

  Subtractor #(.width(1)) subtractor_1 (.b(in_2), .out(out_6), .bin(in_1), .bout(subtractor_1_bout));  // open: a
  Subtractor #(.width(1)) subtractor_2 (
    .b(in_3), .out(out_7), .bin(subtractor_1_bout), .bout(subtractor_2_bout));  // open: a
  Subtractor #(.width(1)) subtractor_3 (
    .b(in_4), .out(out_8), .bin(subtractor_2_bout), .bout(subtractor_3_bout));  // open: a
  Subtractor #(.width(1)) subtractor_4 (.b(in_5), .out(out_9), .bin(subtractor_3_bout));  // open: a, bout
endmodule
