// Logisim project practical4A.circ as structural Verilog: 1 circuit, main circuit main
module main (
  input  A,
  input  E,
  input  F,
  input  B,
  input  G,
  input  C,
  input  H,
  input  D,
  output E_2,
  output A_2,
  output B_2,
  output F_2,
  output C_2,
  output G_2,
  output D_2,
  output H_2
);

  xor xor_1 (F_2, A, B);
  xor xor_2 (G_2, B, C);
  xor xor_3 (H_2, C, D);
  xor xor_4 (B_2, E, F);
  xor xor_5 (C_2, B_2, G);
  xor xor_6 (D_2, C_2, H);

  assign A_2 = E;
  assign E_2 = A;

  // Notes on the sheet:
  //   Binary to Gray (4 bit)
  //   Gray to Binary (4 bit)
endmodule
