// Logisim project practical4B.circ as structural Verilog: 1 circuit, main circuit main
module main (
  input  A,
  input  B,
  input  C,
  output D,
  output E___A__C_B_prime,
  output F___C_A_xor_B,
  output G___BC_prime,
  output H,
  output I
);

  wire not_1_out, not_2_out, or_1_out, xor_1_out;

  not not_1 (not_1_out, B);
  xor xor_1 (xor_1_out, A, B);
  or or_1 (or_1_out, not_1_out, C);
  not not_2 (not_2_out, C);
  and and_1 (D, A, B);
  and and_2 (E___A__C_B_prime, A, or_1_out);
  and and_3 (F___C_A_xor_B, xor_1_out, C);
  and and_4 (G___BC_prime, B, not_2_out);

  assign H = 1'b0;
  assign I = C;
endmodule
