// Logisim project practical4C.circ as structural Verilog: 1 circuit, main circuit main
module main (
  input  A,
  input  B,
  input  C,
  input  D,
  output E___A___BC___BD,
  output F___B_prime_D___B_prime_C___C_prime_D_prime_B,
  output G___C_xor_D,
  output H
);

  wire and_1_out, and_2_out, and_3_out, and_4_out, and_5_out, not_1_out, not_2_out, not_3_out;

  not not_1 (not_1_out, B);
  not not_2 (not_2_out, C);
  and and_1 (and_1_out, B, C);
  and and_2 (and_2_out, B, D);
  not not_3 (not_3_out, D);
  and and_3 (and_3_out, not_1_out, C);
  and and_4 (and_4_out, not_1_out, D);
  and and_5 (and_5_out, B, not_2_out, not_3_out);
  xor xor_1 (G___C_xor_D, D, C);
  or or_1 (E___A___BC___BD, A, and_1_out, and_2_out);
  or or_2 (F___B_prime_D___B_prime_C___C_prime_D_prime_B, and_3_out, and_4_out, and_5_out);

  assign H = D;
endmodule
