// Logisim project practical4D.circ as structural Verilog: 1 circuit, main circuit main
module main (
  input  A,
  input  B,
  input  C,
  input  D,
  output E___A,
  output F___A_prime_B___A_prime_D___A_prime_C___BCD,
  output G___AC_prime_D_prime___ACD___AC_prime_D___A_prime_CD_prime,
  output H___D
);

  wire and_1_out, and_2_out, and_3_out, and_4_out, and_5_out, and_6_out, and_7_out, and_8_out, not_1_out,
       not_2_out, not_3_out;

  not not_1 (not_1_out, A);
  not not_2 (not_2_out, C);
  not not_3 (not_3_out, D);
  and and_1 (and_1_out, not_1_out, B);
  and and_2 (and_2_out, not_1_out, D);
  and and_3 (and_3_out, not_1_out, C);
  and and_4 (and_4_out, B, D, C);
  and and_5 (and_5_out, A, not_3_out, not_2_out);
  and and_6 (and_6_out, A, C, D);
  and and_7 (and_7_out, not_1_out, not_2_out, D);
  and and_8 (and_8_out, not_1_out, C, not_3_out);
  or or_1 (F___A_prime_B___A_prime_D___A_prime_C___BCD, and_1_out, and_2_out, and_3_out, and_4_out);
  or or_2 (G___AC_prime_D_prime___ACD___AC_prime_D___A_prime_CD_prime, and_5_out, and_6_out, and_7_out, and_8_out);

  assign E___A = A;
  assign H___D = D;
endmodule
