// Logisim project practical4c(rough).circ as structural Verilog: 1 circuit, main circuit main
module main (
  input  A,
  input  B,
  input  C,
  input  D,
  output E___AB_prime___AC_prime_D_prime___A_prime_BD,
  output F___B_prime_D___D_prime_C_xor_B,
  output G____A_prime_B_prime__C_xor_D,
  output H
);

  wire and_1_out, and_2_out, and_3_out, and_4_out, and_6_out, and_7_out, not_1_out, not_2_out, not_3_out,
       not_4_out, not_5_out, or_1_out, xor_1_out, xor_2_out;

  not not_1 (not_1_out, A);
  not not_2 (not_2_out, B);
  not not_3 (not_3_out, C);
  and and_1 (and_1_out, A, not_2_out);
  not not_4 (not_4_out, D);
  not not_5 (not_5_out, D);
  xor xor_1 (xor_1_out, B, C);
  or or_1 (or_1_out, not_1_out, not_2_out);
  xor xor_2 (xor_2_out, C, D);
  and and_2 (and_2_out, A, not_4_out, not_3_out);
  and and_3 (and_3_out, not_2_out, D);
  and and_4 (and_4_out, not_5_out, xor_1_out);
  and and_5 (G____A_prime_B_prime__C_xor_D, or_1_out, xor_2_out);
  and and_6 (and_6_out, not_1_out, B, D);
  and and_7 (and_7_out, not_1_out, B, C);
  or or_2 (F___B_prime_D___D_prime_C_xor_B, and_3_out, and_4_out);
  or or_3 (E___AB_prime___AC_prime_D_prime___A_prime_BD, and_6_out, and_1_out, and_7_out, and_2_out);

  assign H = D;
endmodule
