// Logisim project practical5(2).circ as structural Verilog: 1 circuit, main circuit main
module main (
  input  [3:0] A,
  input  [3:0] B,
  output [3:0] out_3,
  output [3:0] out_4
);

  wire [3:0] adder_1_out;
  wire [3:3] not_1_out;

  Adder #(.width(4)) adder_1 (.a(A), .b(B), .out(adder_1_out), .cout(out_4[2]));  // open: cin
  not not_1 (not_1_out[3], out_4[2]);
  Adder #(.width(4)) adder_2 (
    .a(adder_1_out), .b({{2{not_1_out[3]}}, out_4[2], 1'b1}), .out(out_3));  // open: cin, cout

  assign {out_4[3], out_4[1:0]} = 3'b000;

  // Notes on the sheet:
  //   EXCESS-3 PARALLEL ADDER
  //   EXCESS-3 SUM
endmodule
