// Logisim project practical7-19BCE245.circ as structural Verilog: 1 circuit, main circuit main
module main (
  input  S,
  input  R,
  input  D,
  input  J,
  input  K,
  input  T,
  output Q,
  output Q_prime,
  output Q_2,
  output Q_prime_2,
  output Q_3,
  output Q_prime_3,
  output Q_4,
  output Q_prime_4
);

  wire Clock_2_out, Clock_3_out, Clock_4_out, Clock_out, nand_1_out, nand_2_out, nand_3_out, nand_4_out,
       nand_5_out, nand_6_out, nand_7_out, nand_8_out, not_1_out, not_2_out;

  Clock Clock (.out(Clock_out));
  Clock Clock_2 (.out(Clock_2_out));
  Clock Clock_3 (.out(Clock_3_out));
  Clock Clock_4 (.out(Clock_4_out));
  not not_1 (not_1_out, D);
  not not_2 (not_2_out, T);
  nand nand_1 (nand_1_out, S, Clock_out);
  nand nand_2 (nand_2_out, Clock_out, R);
  nand nand_3 (nand_3_out, D, Clock_2_out);
  nand nand_4 (nand_4_out, Clock_2_out, not_1_out);
  nand nand_5 (nand_5_out, J, Q_prime_3, Clock_3_out);
  nand nand_6 (nand_6_out, Clock_3_out, Q_3, K);
  nand nand_7 (nand_7_out, T, Q_prime_4, Clock_4_out);
  nand nand_8 (nand_8_out, Clock_4_out, Q_4, not_2_out);
  nand nand_9 (Q, nand_1_out, Q_prime);
  nand nand_10 (Q_prime, Q, nand_2_out);
  nand nand_11 (Q_2, nand_3_out, Q_prime_2);
  nand nand_12 (Q_prime_2, Q_2, nand_4_out);
  nand nand_13 (Q_3, nand_5_out, Q_prime_3);
  nand nand_14 (Q_prime_3, Q_3, nand_6_out);
  nand nand_15 (Q_4, nand_7_out, Q_prime_4);
  nand nand_16 (Q_prime_4, Q_4, nand_8_out);

  // Notes on the sheet:
  //   RS Flip-Flop
  //   D Flip-Flop
  //   JK Flip-Flop
  //   T Flip-Flop
endmodule
