// Logisim project practical 8 - 19BCE245.circ as structural Verilog: 1 circuit, main circuit main
module main (
  input  in_1,
  output out_2,
  output out_3,
  output out_4
);

  wire and_1_out, clock_1_out, undriven;

  Clock clock_1 (.out(clock_1_out));
  J_K_Flip_Flop j_k_ff_1 (.J(in_1), .clk(clock_1_out), .K(in_1), .Q(out_4));  // open: Qn, preset, en, reset
  J_K_Flip_Flop j_k_ff_2 (.J(out_4), .clk(clock_1_out), .K(undriven), .Q(out_3));  // open: Qn, preset, en, reset
  and and_1 (and_1_out, undriven, out_3);
  J_K_Flip_Flop j_k_ff_3 (.J(and_1_out), .clk(clock_1_out), .K(and_1_out), .Q(out_2));  // open: Qn, preset, en, reset
endmodule
