// Logisim project 19BCE245_Prac-9.circ as structural Verilog: 1 circuit, main circuit main
module main (
  output A1,
  output A2,
  output A3,
  output A4,
  output A1_2,
  output A2_2,
  output A3_2,
  output A1_3,
  output A2_3,
  output A3_3
);

  wire and_1_out, clock_1_out, clock_2_out, clock_3_out, not_1_out, not_2_out, not_3_out, t_ff_1_qn,
       t_ff_2_qn;

  Clock clock_1 (.out(clock_1_out));
  Clock clock_2 (.out(clock_2_out));
  J_K_Flip_Flop j_k_ff_1 (.J(1'b1), .clk(clock_1_out), .K(1'b1), .Q(A1));  // open: Qn, preset, en, reset
  not not_1 (not_1_out, clock_2_out);
  J_K_Flip_Flop j_k_ff_2 (.J(1'b1), .clk(not_1_out), .K(1'b1), .Q(A1_3));  // open: Qn, preset, en, reset
  J_K_Flip_Flop j_k_ff_3 (.J(1'b1), .clk(A1), .K(1'b1), .Q(A2));  // open: Qn, preset, en, reset
  not not_2 (not_2_out, A1_3);
  J_K_Flip_Flop j_k_ff_4 (.J(1'b1), .clk(not_2_out), .K(1'b1), .Q(A2_3));  // open: Qn, preset, en, reset
  J_K_Flip_Flop j_k_ff_5 (.J(1'b1), .clk(A2), .K(1'b1), .Q(A3));  // open: Qn, preset, en, reset
  not not_3 (not_3_out, A2_3);
  J_K_Flip_Flop j_k_ff_6 (.J(1'b1), .clk(not_3_out), .K(1'b1), .Q(A3_3));  // open: Qn, preset, en, reset
  J_K_Flip_Flop j_k_ff_7 (.J(1'b1), .clk(A3), .K(1'b1), .Q(A4));  // open: Qn, preset, en, reset
  Clock clock_3 (.out(clock_3_out));
  T_Flip_Flop t_ff_1 (.clk(clock_3_out), .T(1'b1), .Q(A3_2), .Qn(t_ff_1_qn), .reset(and_1_out));  // open: preset, en
  and and_1 (and_1_out, A2_2, A1_2);
  T_Flip_Flop t_ff_2 (.clk(t_ff_1_qn), .T(1'b1), .Q(A2_2), .Qn(t_ff_2_qn), .reset(and_1_out));  // open: preset, en
  T_Flip_Flop t_ff_3 (.clk(t_ff_2_qn), .T(1'b1), .Q(A1_2), .reset(and_1_out));  // open: Qn, preset, en

  // Notes on the sheet:
  //   4 BIT BINARY RIPPLE COUNTER
  //   MOD 7 COUNTER - A MOD N COUNTER COUNT FROM 0 TO N-1
  //   MOD 6 RIPPLE COUNTER USING T-FLIPS-FLOPS
endmodule
